# Fritzing sketch Schematic (saved by Fritzing 0.9.4)
breadboards: 1

parts:
  Mod1 = Raspberry Pi Pico W
  LED1 = RGB LED (com. anode, rbg) [package="5 mm [THT]"]
  R1 = Resistor [tolerance=±5% resistance=220 package="2010 [SMD]"]
  R2 = Resistor [tolerance=±5% resistance=220 package="2010 [SMD]"]
  R3 = Resistor [tolerance=±5% resistance=220 package="2010 [SMD]"]
  S1 = Momentary Switch [package=ksa_sealed_tac_switch]
  S2 = Momentary Switch [package=ksa_sealed_tac_switch]
  S3 = Momentary Switch [package=ksa_sealed_tac_switch]
  R4 = Resistor [tolerance=±5% resistance=10k package="2512 [SMD]"]
  R5 = Resistor [tolerance=±5% resistance=10k package="2512 [SMD]"]
  R6 = Resistor [tolerance=±5% resistance=10k package="2512 [SMD]"]
  R7 = Resistor [tolerance=±5% resistance=10k package="2512 [SMD]"]
  R8 = Resistor [tolerance=±5% resistance=10k package="2512 [SMD]"]
  R9 = Resistor [tolerance=±5% resistance=10k package="2512 [SMD]"]
  DHT1 = DHT11 Humitidy and Temperature Sensor
  R10 = Resistor [tolerance=±5% resistance=10k package="2512 [SMD]"]

nets:
  N1: Mod1.pin_3, Mod1.pin_8, Mod1.pin_13, Mod1.pin_18, Mod1.pin_23, Mod1.pin_28, Mod1.pin_33, Mod1.pin_38, Mod1.pin_42, S1.2, S2.2, S3.2, DHT1.GND
  N2: Mod1.pin_10, R7.Pin_0
  N3: Mod1.pin_11, R8.Pin_0
  N4: Mod1.pin_12, R9.Pin_0
  N5: Mod1.pin_15, R1.Pin_1
  N6: Mod1.pin_16, R2.Pin_1
  N7: Mod1.pin_17, R3.Pin_1
  N8: Mod1.pin_20, DHT1.DATA
  N9: Mod1.pin_36, LED1.common_anode, R4.Pin_0, R5.Pin_0, R6.Pin_0, R10.Pin_0
  N10: LED1.red_cathode, R3.Pin_0
  N11: LED1.blue_cathode, R2.Pin_0
  N12: LED1.green_cathode, R1.Pin_0
  N13: S1.3, R6.Pin_1
  N14: S1.4, R7.Pin_1
  N15: S2.3, R5.Pin_1
  N16: S2.4, R8.Pin_1
  N17: S3.3, R4.Pin_1
  N18: S3.4, R9.Pin_1
  N19: DHT1.VDD, R10.Pin_1

custom parts:
  Raspberry Pi Pico W: Raspberry Pi Pico W. Based around the RP2040 microcontroller the Pico W is a low cost microcontroller device bringing Raspberry Pi quality, cost, and easy of use to the microcontroller space. The areas marked KEEPOUT in pcb silkscreen should not have traces running through them to avoid shorts on a soldered in module!
  DHT11 Humitidy and Temperature Sensor: DHT11 Humidity and Temperature Sensor
